// Logisim project CP0.circ as structural Verilog: 1 circuit, main circuit CP0
module CP0 (
  input  Expsrc0,
  input  clk,
  input  Expsrc1,
  input  Enable,
  input  Expsrc2,
  input  [31:0] Inst,
  input  [31:0] PCin,
  input  [31:0] Din,
  output ExRegWrite,
  output HasExp,
  output IsRet,
  output ExpBlock,
  output [31:0] PCout,
  output [31:0] Dout
);

  wire and_4_out, and_5_out, and_6_out, and_7_out, BlockSrc0, BlockSrc1, BlockSrc2, counter_1_q, counter_2_q,
       demultiplexer_1_out0, demultiplexer_1_out1, demultiplexer_2_out0, demultiplexer_2_out1,
       demultiplexer_3_out0, demultiplexer_3_out1, demultiplexer_4_out0, demultiplexer_4_out1,
       demultiplexer_4_out2, ExpClick, not_2_out, not_3_out, or_1_out, or_2_out;
  wire [31:0] Cause_q, controlled_buffer_1_out, multiplexer_1_out;
  wire [31:1] Status_q;
  wire [31:3] Block_Reg_q;

  Demultiplexer demultiplexer_1 (
    .out0(demultiplexer_1_out0), .out1(demultiplexer_1_out1), .in(Expsrc0), .sel(BlockSrc0));
  and and_1 (ExpClick, or_1_out, ~ExpBlock);  // AND_Gate
  or or_1 (or_1_out, demultiplexer_1_out0, demultiplexer_2_out0, demultiplexer_3_out0);
  Demultiplexer demultiplexer_2 (
    .out0(demultiplexer_2_out0), .out1(demultiplexer_2_out1), .in(Expsrc1), .sel(BlockSrc1));
  not not_1 (ExRegWrite, Inst[23]);
  Counter #(.max('h1), .ongoal("stay"), .width(1)) counter_1 (
    .Q(counter_1_q), .clk(ExpClick), .clr(counter_2_q));  // open: load, D, count, carry, up
  and and_2 (IsRet, ~Inst[5], Inst[4], Inst[3], ~Inst[2], ~Inst[1], ~Inst[0]);  // AND_Gate
  Demultiplexer demultiplexer_3 (
    .out0(demultiplexer_3_out0), .out1(demultiplexer_3_out1), .in(Expsrc2), .sel(BlockSrc2));
  and and_3 (HasExp, clk, counter_1_q);
  Counter #(.max('h1), .ongoal("stay"), .trigger("falling"), .width(1)) counter_2 (
    .Q(counter_2_q), .clk(HasExp), .clr(not_2_out));  // open: load, D, count, carry, up
  not not_2 (not_2_out, counter_1_q);
  not not_3 (not_3_out, HasExp);
  assign controlled_buffer_1_out = Expsrc0 ? 32'h1 : 32'bz;  // Controlled_Buffer controlled_buffer_1
  assign controlled_buffer_1_out = Expsrc1 ? 32'h3 : 32'bz;  // Controlled_Buffer controlled_buffer_2
  assign controlled_buffer_1_out = Expsrc2 ? 32'h7 : 32'bz;  // Controlled_Buffer controlled_buffer_3
  Multiplexer #(.width(32)) multiplexer_1 (.in0(PCin), .in1(Din), .out(multiplexer_1_out), .sel(not_3_out));
  and and_4 (and_4_out, Enable, ~ExRegWrite);  // AND_Gate
  Demultiplexer #(.select(2)) demultiplexer_4 (
    .out0(demultiplexer_4_out0), .out1(demultiplexer_4_out1), .out2(demultiplexer_4_out2), .in(1'b1),
    .sel(Inst[12:11]));  // open: out3
  and and_5 (and_5_out, demultiplexer_4_out0, and_4_out);
  and and_6 (and_6_out, demultiplexer_4_out1, and_4_out);
  and and_7 (and_7_out, demultiplexer_4_out2, and_4_out);
  or or_2 (or_2_out, HasExp, and_5_out);
  Register #(.width(32)) Status (.D(Din), .en(and_6_out), .Q({Status_q, ExpBlock}), .clk(clk));  // open: clr
  Register #(.width(32)) Block_Reg (
    .en(and_7_out), .Q({Block_Reg_q, BlockSrc2, BlockSrc1, BlockSrc0}), .clk(clk));  // open: D, clr
  Register #(.width(32)) Cause (.D(controlled_buffer_1_out), .Q(Cause_q), .clk(ExpClick));  // open: en, clr
  Register #(.trigger("falling"), .width(32)) EPC_Reg (
    .D(multiplexer_1_out), .en(or_2_out), .Q(PCout));  // open: clk, clr
  Multiplexer #(.select(2), .width(32)) multiplexer_2 (
    .in0(PCout), .in1({Status_q, ExpBlock}), .in2({Block_Reg_q, BlockSrc2, BlockSrc1, BlockSrc0}),
    .in3(Cause_q), .out(Dout), .sel(Inst[12:11]));
  // also tied to GND on the sheet: {demultiplexer_1_out1, demultiplexer_2_out1, demultiplexer_3_out1}

  // Other names for the same wires on the sheet: Sel[1:0] = Inst[12:11]

  // Notes on the sheet:
  //   Signal Decoding
  //   Exception Signals
  //   Input & Ouput
  //   Registers
endmodule
