// Logisim project ALU_Decoder.circ as structural Verilog: 1 circuit, main circuit ALU_Decoder
module ALU_Decoder (
  input  Op5,
  input  Op4,
  input  Op3,
  input  Op2,
  input  Op1,
  input  Op0,
  output ALUop3,
  output ALUop2,
  output ALUop1,
  output ALUop0
);

  wire and_1_out, and_2_out, and_3_out, and_4_out, and_5_out, and_6_out, and_7_out, and_8_out, and_9_out,
       and_10_out, and_11_out, and_12_out, and_13_out, and_14_out, not_1_out, not_2_out, not_3_out,
       not_4_out, not_5_out, not_6_out;

  not not_1 (not_1_out, Op5);
  not not_2 (not_2_out, Op4);
  not not_3 (not_3_out, Op3);
  not not_4 (not_4_out, Op2);
  not not_5 (not_5_out, Op1);
  not not_6 (not_6_out, Op0);
  and and_1 (and_1_out, not_1_out, not_2_out, Op3, Op1, not_6_out);
  or or_1 (ALUop3, and_1_out, and_2_out);
  and and_2 (and_2_out, not_1_out, not_2_out, Op3, Op2, not_5_out, Op0);
  and and_3 (and_3_out, not_2_out, not_3_out, not_4_out, Op1, Op0);
  and and_4 (and_4_out, not_1_out, not_2_out, not_3_out, Op2, not_5_out);
  and and_5 (and_5_out, not_1_out, not_2_out, Op3, not_4_out, not_5_out);
  and and_6 (and_6_out, not_1_out, not_2_out, not_5_out, not_6_out);
  and and_7 (and_7_out, not_1_out, not_2_out, not_3_out, not_4_out, not_6_out);
  and and_8 (and_8_out, not_1_out, not_2_out, Op3, not_4_out, Op1, not_6_out);
  or or_2 (ALUop1, and_8_out, and_9_out);
  and and_9 (and_9_out, not_1_out, not_2_out, Op3, Op2, not_5_out, not_6_out);
  and and_10 (and_10_out, not_2_out, not_3_out, not_4_out, Op1, Op0);
  and and_11 (and_11_out, not_1_out, not_2_out, not_3_out, Op2, not_5_out);
  and and_12 (and_12_out, not_1_out, not_2_out, Op3, not_4_out, not_5_out);
  and and_13 (and_13_out, not_1_out, not_2_out, Op3, not_6_out);
  and and_14 (and_14_out, not_1_out, not_2_out, not_4_out, not_6_out);
  or or_3 (ALUop2, and_3_out, and_4_out, and_5_out, and_6_out, and_7_out);
  or or_4 (ALUop0, and_10_out, and_11_out, and_12_out, and_13_out, and_14_out);
endmodule
