// Logisim project Control_Unit.circ as structural Verilog: 3 circuits, main circuit Control_Unit
module ALU_decoder (
  input  [5:0] Op,
  output [3:0] ALUOp
);

  wire and_1_out, and_2_out, and_3_out, and_4_out, and_5_out, and_6_out, and_7_out, and_8_out, and_9_out,
       and_10_out, and_11_out, and_12_out, and_13_out, and_14_out, not_1_out, not_2_out, not_3_out,
       not_4_out, not_5_out, not_6_out;

  not not_1 (not_1_out, Op[5]);
  not not_2 (not_2_out, Op[4]);
  not not_3 (not_3_out, Op[3]);
  not not_4 (not_4_out, Op[2]);
  not not_5 (not_5_out, Op[1]);
  not not_6 (not_6_out, Op[0]);
  and and_1 (and_1_out, not_1_out, not_2_out, Op[3], Op[1], not_6_out);
  and and_2 (and_2_out, not_1_out, not_2_out, Op[3], Op[2], not_5_out, Op[0]);
  and and_3 (and_3_out, not_2_out, not_3_out, not_4_out, Op[1], Op[0]);
  and and_4 (and_4_out, not_1_out, not_2_out, not_3_out, Op[2], not_5_out);
  and and_5 (and_5_out, not_1_out, not_2_out, Op[3], not_4_out, not_5_out);
  and and_6 (and_6_out, not_1_out, not_2_out, not_5_out, not_6_out);
  and and_7 (and_7_out, not_1_out, not_2_out, not_3_out, not_4_out, not_6_out);
  and and_8 (and_8_out, not_1_out, not_2_out, Op[3], not_4_out, Op[1], not_6_out);
  and and_9 (and_9_out, not_1_out, not_2_out, Op[3], Op[2], not_5_out, not_6_out);
  and and_10 (and_10_out, not_2_out, not_3_out, not_4_out, Op[1], Op[0]);
  and and_11 (and_11_out, not_1_out, not_2_out, not_3_out, Op[2], not_5_out);
  and and_12 (and_12_out, not_1_out, not_2_out, Op[3], not_4_out, not_5_out);
  and and_13 (and_13_out, not_1_out, not_2_out, Op[3], not_6_out);
  and and_14 (and_14_out, not_1_out, not_2_out, not_4_out, not_6_out);
  or or_1 (ALUOp[3], and_1_out, and_2_out);
  or or_2 (ALUOp[2], and_3_out, and_4_out, and_5_out, and_6_out, and_7_out);
  or or_3 (ALUOp[1], and_8_out, and_9_out);
  or or_4 (ALUOp[0], and_10_out, and_11_out, and_12_out, and_13_out, and_14_out);
endmodule

module Control_Unit (
  input  [5:0] op,
  input  [5:0] funct,
  output isCOP0,
  output [3:0] ALUOp,
  output isJr,
  output isSyscall,
  output isShamt,
  output MemRead,
  output MemWrite,
  output ALUSrc,
  output Jump,
  output MemtoReg,
  output Branch,
  output RegDst,
  output RegWrite,
  output BneBeq,
  output isJAL,
  output ZeroExtend,
  output ReadRs,
  output ReadRt
);

  ALU_Decoding_Area alu_decoding_area_1 (
    .op(op), .Funct(funct), .isCOP0(isCOP0), .ALUOp(ALUOp), .isJr(isJr), .isSyscall(isSyscall),
    .isShamt(isShamt));
  Opcode_decoder opcode_decoder_1 (
    .op0(op[0]), .op1(op[1]), .op2(op[2]), .op3(op[3]), .op4(op[4]), .op5(op[5]), .MemRead(MemRead),
    .MemWrite(MemWrite), .ALUSrc(ALUSrc), .Jump(Jump), .MemtoReg(MemtoReg), .Branch(Branch), .RegDst(RegDst),
    .RegWrite(RegWrite), .BneBeq(BneBeq), .IsJAL(isJAL), .ZeroExtend(ZeroExtend));
  RegisterRead_Detector registerread_detector_1 (
    .op0(op[0]), .op1(op[1]), .op2(op[2]), .op3(op[3]), .op4(op[4]), .op5(op[5]), .Funct0(funct[0]),
    .Funct1(funct[1]), .Funct2(funct[2]), .Funct3(funct[3]), .Funct4(funct[4]), .Funct5(funct[5]),
    .ReadRs(ReadRs), .ReadRt(ReadRt));
endmodule

module ALU_Decoding_Area (
  input  [5:0] op,
  input  [5:0] Funct,
  output isCOP0,
  output [3:0] ALUOp,
  output isJr,
  output isSyscall,
  output isShamt
);

  wire funct_decoder_1_isjr, funct_decoder_1_isshamt, funct_decoder_1_issyscall, multiplexer_4_out, special;
  wire [3:0] alu_decoder_1_aluop, funct_decoder_1_alu0;

  ALU_decoder alu_decoder_1 (.Op(op), .ALUOp(alu_decoder_1_aluop));
  Funct_Decoder funct_decoder_1 (
    .Funct0(Funct[0]), .Funct1(Funct[1]), .Funct2(Funct[2]), .Funct3(Funct[3]), .Funct4(Funct[4]),
    .Funct5(Funct[5]), .ALU0(funct_decoder_1_alu0[0]), .ALU1(funct_decoder_1_alu0[1]),
    .ALU2(funct_decoder_1_alu0[2]), .ALU3(funct_decoder_1_alu0[3]), .IsJR(funct_decoder_1_isjr),
    .IsSyscall(funct_decoder_1_issyscall), .IsShamt(funct_decoder_1_isshamt));
  and and_1 (isCOP0, ~op[0], ~op[1], ~op[2], ~op[3], op[4], ~op[5]);  // AND_Gate
  and and_2 (special, ~op[0], ~op[1], ~op[2], ~op[3], op[4], ~op[5]);  // AND_Gate
  Multiplexer #(.width(4)) multiplexer_1 (
    .in0(alu_decoder_1_aluop), .in1(funct_decoder_1_alu0), .out(ALUOp), .sel(special));
  Multiplexer multiplexer_2 (.in0(1'b0), .in1(funct_decoder_1_isjr), .out(isJr), .sel(special));
  Multiplexer multiplexer_3 (.in0(1'b0), .in1(funct_decoder_1_issyscall), .out(isSyscall), .sel(special));
  Multiplexer multiplexer_4 (.in0(1'b0), .in1(funct_decoder_1_isshamt), .out(multiplexer_4_out), .sel(special));
  not not_1 (isShamt, multiplexer_4_out);
endmodule
