// Logisim project Funct_Decoder.circ as structural Verilog: 1 circuit, main circuit Funct_Decoder
module Funct_Decoder (
  input  Funct0,
  input  Funct1,
  input  Funct2,
  input  Funct3,
  input  Funct4,
  input  Funct5,
  output ALU0,
  output ALU1,
  output ALU2,
  output ALU3,
  output IsJR,
  output IsSyscall,
  output IsShamt
);

  wire and_1_out, and_2_out, and_3_out, and_4_out, and_5_out, and_6_out, and_7_out, and_8_out, and_9_out,
       and_10_out, and_11_out, and_12_out, and_13_out, and_14_out, and_15_out, and_16_out, and_17_out,
       and_20_out, and_21_out, and_22_out, not_1_out, not_2_out, not_3_out, not_4_out, not_5_out, not_6_out,
       not_7_out, not_8_out, not_9_out, not_10_out, not_11_out, not_12_out, not_13_out, not_14_out,
       not_15_out, not_16_out, not_17_out, not_18_out, not_19_out, not_20_out, not_21_out, not_22_out,
       not_23_out, not_24_out, not_25_out, not_26_out, not_27_out, not_28_out, not_29_out, not_30_out,
       not_31_out, not_32_out, not_33_out, not_34_out, not_35_out, not_36_out, not_37_out, not_38_out,
       not_39_out, not_40_out, not_41_out, not_42_out, not_43_out, not_44_out, not_45_out, not_46_out,
       not_47_out, not_48_out, not_49_out, not_50_out, not_51_out, not_52_out, not_53_out, not_54_out,
       not_55_out, not_56_out, not_57_out, not_58_out, not_59_out, not_60_out, not_61_out, not_62_out,
       not_63_out, not_64_out, not_65_out, not_66_out, not_67_out, not_68_out, not_69_out, not_70_out,
       not_71_out, not_72_out, not_73_out, not_74_out, not_75_out, not_76_out, not_77_out, not_78_out,
       not_79_out, not_80_out, not_81_out;

  not not_1 (not_1_out, Funct1);
  not not_2 (not_2_out, Funct2);
  not not_3 (not_3_out, Funct4);
  not not_4 (not_4_out, Funct1);
  not not_5 (not_5_out, Funct2);
  not not_6 (not_6_out, Funct1);
  not not_7 (not_7_out, Funct3);
  not not_8 (not_8_out, Funct5);
  not not_9 (not_9_out, Funct1);
  not not_10 (not_10_out, Funct3);
  not not_11 (not_11_out, Funct1);
  not not_12 (not_12_out, Funct2);
  not not_13 (not_13_out, Funct3);
  not not_14 (not_14_out, Funct4);
  not not_15 (not_15_out, Funct1);
  not not_16 (not_16_out, Funct2);
  not not_17 (not_17_out, Funct3);
  not not_18 (not_18_out, Funct5);
  not not_19 (not_19_out, Funct1);
  not not_20 (not_20_out, Funct2);
  not not_21 (not_21_out, Funct4);
  not not_22 (not_22_out, Funct5);
  not not_23 (not_23_out, Funct1);
  not not_24 (not_24_out, Funct3);
  not not_25 (not_25_out, Funct1);
  not not_26 (not_26_out, Funct2);
  not not_27 (not_27_out, Funct3);
  not not_28 (not_28_out, Funct5);
  not not_29 (not_29_out, Funct1);
  not not_30 (not_30_out, Funct2);
  not not_31 (not_31_out, Funct4);
  not not_32 (not_32_out, Funct5);
  not not_33 (not_33_out, Funct0);
  not not_34 (not_34_out, Funct1);
  not not_35 (not_35_out, Funct2);
  not not_36 (not_36_out, Funct3);
  not not_37 (not_37_out, Funct5);
  not not_38 (not_38_out, Funct1);
  not not_39 (not_39_out, Funct2);
  not not_40 (not_40_out, Funct1);
  not not_41 (not_41_out, Funct3);
  not not_42 (not_42_out, Funct5);
  not not_43 (not_43_out, Funct0);
  not not_44 (not_44_out, Funct1);
  not not_45 (not_45_out, Funct2);
  not not_46 (not_46_out, Funct3);
  not not_47 (not_47_out, Funct1);
  not not_48 (not_48_out, Funct2);
  not not_49 (not_49_out, Funct3);
  not not_50 (not_50_out, Funct4);
  not not_51 (not_51_out, Funct1);
  not not_52 (not_52_out, Funct2);
  not not_53 (not_53_out, Funct4);
  not not_54 (not_54_out, Funct5);
  not not_55 (not_55_out, Funct1);
  not not_56 (not_56_out, Funct3);
  not not_57 (not_57_out, Funct5);
  not not_58 (not_58_out, Funct0);
  not not_59 (not_59_out, Funct1);
  not not_60 (not_60_out, Funct3);
  not not_61 (not_61_out, Funct4);
  not not_62 (not_62_out, Funct5);
  not not_63 (not_63_out, Funct0);
  not not_64 (not_64_out, Funct1);
  not not_65 (not_65_out, Funct4);
  not not_66 (not_66_out, Funct5);
  not not_67 (not_67_out, Funct0);
  not not_68 (not_68_out, Funct1);
  not not_69 (not_69_out, Funct2);
  not not_70 (not_70_out, Funct3);
  not not_71 (not_71_out, Funct0);
  not not_72 (not_72_out, Funct1);
  not not_73 (not_73_out, Funct2);
  not not_74 (not_74_out, Funct3);
  not not_75 (not_75_out, Funct5);
  not not_76 (not_76_out, Funct0);
  not not_77 (not_77_out, Funct1);
  not not_78 (not_78_out, Funct2);
  not not_79 (not_79_out, Funct3);
  not not_80 (not_80_out, Funct4);
  not not_81 (not_81_out, Funct5);
  and and_1 (and_1_out, Funct0, not_1_out, not_2_out, Funct3, not_3_out, Funct5);
  and and_2 (and_2_out, Funct0, not_4_out, not_5_out, Funct3, Funct4, Funct5);
  and and_3 (and_3_out, Funct0, not_6_out, Funct2, not_7_out, Funct4, not_8_out);
  and and_4 (and_4_out, Funct0, not_9_out, Funct2, not_10_out, Funct4, Funct5);
  and and_5 (and_5_out, Funct0, not_11_out, not_12_out, not_13_out, not_14_out);
  and and_6 (and_6_out, Funct0, not_15_out, not_16_out, not_17_out, not_18_out);
  and and_7 (and_7_out, Funct0, not_19_out, not_20_out, not_21_out, not_22_out);
  and and_8 (and_8_out, Funct0, not_23_out, Funct2, not_24_out, Funct4, Funct5);
  and and_9 (and_9_out, Funct0, not_25_out, not_26_out, not_27_out, Funct4, not_28_out);
  and and_10 (and_10_out, Funct0, not_29_out, not_30_out, Funct3, not_31_out, not_32_out);
  and and_11 (and_11_out, not_33_out, not_34_out, not_35_out, not_36_out, Funct4, not_37_out);
  and and_12 (and_12_out, Funct0, not_38_out, not_39_out, Funct3, Funct4, Funct5);
  and and_13 (and_13_out, Funct0, not_40_out, Funct2, not_41_out, Funct4, not_42_out);
  and and_14 (and_14_out, not_43_out, not_44_out, not_45_out, not_46_out, Funct4, Funct5);
  and and_15 (and_15_out, Funct0, not_47_out, not_48_out, not_49_out, not_50_out);
  and and_16 (and_16_out, Funct0, not_51_out, not_52_out, not_53_out, not_54_out);
  and and_17 (and_17_out, Funct0, not_55_out, Funct2, not_56_out, Funct4, not_57_out);
  and and_18 (IsJR, not_58_out, not_59_out, Funct2, not_60_out, not_61_out, not_62_out);
  and and_19 (IsSyscall, not_63_out, not_64_out, Funct2, Funct3, not_65_out, not_66_out);
  and and_20 (and_20_out, not_67_out, not_68_out, not_69_out, not_70_out, Funct4, Funct5);
  and and_21 (and_21_out, not_71_out, not_72_out, not_73_out, not_74_out, Funct4, not_75_out);
  and and_22 (and_22_out, not_76_out, not_77_out, not_78_out, not_79_out, not_80_out, not_81_out);
  or or_1 (ALU0, and_1_out, and_2_out, and_3_out, and_4_out);
  or or_2 (ALU1, and_5_out, and_6_out, and_7_out, and_8_out);
  or or_3 (ALU2, and_9_out, and_10_out, and_11_out, and_12_out, and_13_out);
  or or_4 (ALU3, and_14_out, and_15_out, and_16_out, and_17_out);
  or or_5 (IsShamt, and_20_out, and_21_out, and_22_out);
endmodule
