// Logisim project Immediate_Extender.circ as structural Verilog: 1 circuit, main circuit immediate_extender
module immediate_extender (
  input  ZeroExtend,
  input  [15:0] Imme_Value,
  output [31:0] result
);

  wire [31:0] bit_extender_1_out, bit_extender_2_out;

  assign bit_extender_1_out = {{16{Imme_Value[15]}}, Imme_Value};  // Bit_Extender bit_extender_1
  assign bit_extender_2_out = {{16{1'b0}}, Imme_Value};  // Bit_Extender bit_extender_2
  Multiplexer #(.width(32)) multiplexer_1 (
    .in0(bit_extender_1_out), .in1(bit_extender_2_out), .out(result), .sel(ZeroExtend));
endmodule
