// Logisim project RegFile.circ as structural Verilog: 1 circuit, main circuit regfile
module regfile (
  input  [4:0] R1A,
  input  [4:0] R2A,
  input  [4:0] RW,
  input  [31:0] Din,
  input  we,
  input  clk,
  output [31:0] R1,
  output [31:0] a0,
  output [31:0] v0,
  output [31:0] R2
);

  wire demultiplexer_1_out0, demultiplexer_1_out1, demultiplexer_1_out2, demultiplexer_1_out3,
       demultiplexer_2_out0, demultiplexer_2_out1, demultiplexer_2_out2, demultiplexer_2_out3,
       demultiplexer_2_out4, demultiplexer_2_out5, demultiplexer_2_out6, demultiplexer_2_out7,
       demultiplexer_3_out0, demultiplexer_3_out1, demultiplexer_3_out2, demultiplexer_3_out3,
       demultiplexer_3_out4, demultiplexer_3_out5, demultiplexer_3_out6, demultiplexer_3_out7,
       demultiplexer_4_out0, demultiplexer_4_out1, demultiplexer_4_out2, demultiplexer_4_out3,
       demultiplexer_4_out4, demultiplexer_4_out5, demultiplexer_4_out6, demultiplexer_4_out7,
       demultiplexer_5_out0, demultiplexer_5_out1, demultiplexer_5_out2, demultiplexer_5_out3,
       demultiplexer_5_out4, demultiplexer_5_out5, demultiplexer_5_out6, demultiplexer_5_out7;
  wire [31:0] ra, register_2_q, register_3_q, register_4_q, register_5_q, register_6_q, register_8_q,
       register_10_q, register_12_q, register_13_q, register_14_q, register_15_q, register_16_q,
       register_17_q, register_18_q, register_19_q, register_20_q, register_21_q, register_22_q,
       register_23_q, register_24_q, register_25_q, register_26_q, register_27_q, register_28_q,
       register_29_q, register_30_q, register_32_q, s0, s1, s2;

  Demultiplexer #(.enable("true"), .select(2)) demultiplexer_1 (
    .out0(demultiplexer_1_out0), .out1(demultiplexer_1_out1), .out2(demultiplexer_1_out2),
    .out3(demultiplexer_1_out3), .in(1'b1), .sel(RW[4:3]), .en(we));
  Demultiplexer #(.enable("true"), .select(3)) demultiplexer_2 (
    .out0(demultiplexer_2_out0), .out1(demultiplexer_2_out1), .out2(demultiplexer_2_out2),
    .out3(demultiplexer_2_out3), .out4(demultiplexer_2_out4), .out5(demultiplexer_2_out5),
    .out6(demultiplexer_2_out6), .out7(demultiplexer_2_out7), .in(1'b1), .sel(RW[2:0]),
    .en(demultiplexer_1_out0));
  Demultiplexer #(.enable("true"), .select(3)) demultiplexer_3 (
    .out0(demultiplexer_3_out0), .out1(demultiplexer_3_out1), .out2(demultiplexer_3_out2),
    .out3(demultiplexer_3_out3), .out4(demultiplexer_3_out4), .out5(demultiplexer_3_out5),
    .out6(demultiplexer_3_out6), .out7(demultiplexer_3_out7), .in(1'b1), .sel(RW[2:0]),
    .en(demultiplexer_1_out1));
  Demultiplexer #(.enable("true"), .select(3)) demultiplexer_4 (
    .out0(demultiplexer_4_out0), .out1(demultiplexer_4_out1), .out2(demultiplexer_4_out2),
    .out3(demultiplexer_4_out3), .out4(demultiplexer_4_out4), .out5(demultiplexer_4_out5),
    .out6(demultiplexer_4_out6), .out7(demultiplexer_4_out7), .in(1'b1), .sel(RW[2:0]),
    .en(demultiplexer_1_out2));
  Demultiplexer #(.enable("true"), .select(3)) demultiplexer_5 (
    .out0(demultiplexer_5_out0), .out1(demultiplexer_5_out1), .out2(demultiplexer_5_out2),
    .out3(demultiplexer_5_out3), .out4(demultiplexer_5_out4), .out5(demultiplexer_5_out5),
    .out6(demultiplexer_5_out6), .out7(demultiplexer_5_out7), .in(1'b1), .sel(RW[2:0]),
    .en(demultiplexer_1_out3));
  Register #(.width(32)) register_1 (.D(Din), .en(demultiplexer_4_out0), .Q(s0), .clk(clk));  // open: clr
  Register #(.width(32)) register_2 (.D(Din), .en(demultiplexer_5_out0), .Q(register_2_q), .clk(clk));  // open: clr
  Register #(.width(32)) register_3 (.D(Din), .en(demultiplexer_2_out0), .Q(register_3_q));  // open: clk, clr
  Register #(.width(32)) register_4 (.D(Din), .en(demultiplexer_3_out0), .Q(register_4_q), .clk(clk));  // open: clr
  Register #(.width(32)) register_5 (.D(Din), .en(demultiplexer_2_out1), .Q(register_5_q), .clk(clk));  // open: clr
  Register #(.width(32)) register_6 (.D(Din), .en(demultiplexer_3_out1), .Q(register_6_q), .clk(clk));  // open: clr
  Register #(.width(32)) register_7 (.D(Din), .en(demultiplexer_4_out1), .Q(s1), .clk(clk));  // open: clr
  Register #(.width(32)) register_8 (.D(Din), .en(demultiplexer_5_out1), .Q(register_8_q), .clk(clk));  // open: clr
  Register #(.width(32)) register_9 (.D(Din), .en(demultiplexer_4_out2), .Q(s2), .clk(clk));  // open: clr
  Register #(.width(32)) register_10 (.D(Din), .en(demultiplexer_5_out2), .Q(register_10_q), .clk(clk));  // open: clr
  Register #(.width(32)) register_11 (.D(Din), .en(demultiplexer_2_out2), .Q(v0), .clk(clk));  // open: clr
  Register #(.width(32)) register_12 (.D(Din), .en(demultiplexer_3_out2), .Q(register_12_q), .clk(clk));  // open: clr
  Register #(.width(32)) register_13 (.D(Din), .en(demultiplexer_2_out3), .Q(register_13_q), .clk(clk));  // open: clr
  Register #(.width(32)) register_14 (.D(Din), .en(demultiplexer_3_out3), .Q(register_14_q), .clk(clk));  // open: clr
  Register #(.width(32)) register_15 (.D(Din), .en(demultiplexer_4_out3), .Q(register_15_q), .clk(clk));  // open: clr
  Register #(.width(32)) register_16 (.D(Din), .en(demultiplexer_5_out3), .Q(register_16_q), .clk(clk));  // open: clr
  Register #(.width(32)) register_17 (.D(Din), .en(demultiplexer_2_out4), .Q(register_17_q), .clk(clk));  // open: clr
  Register #(.width(32)) register_18 (.D(Din), .en(demultiplexer_3_out4), .Q(register_18_q), .clk(clk));  // open: clr
  Register #(.width(32)) register_19 (.D(Din), .en(demultiplexer_4_out4), .Q(register_19_q), .clk(clk));  // open: clr
  Register #(.width(32)) register_20 (.D(Din), .en(demultiplexer_5_out4), .Q(register_20_q), .clk(clk));  // open: clr
  Register #(.width(32)) register_21 (.D(Din), .en(demultiplexer_3_out5), .Q(register_21_q), .clk(clk));  // open: clr
  Register #(.width(32)) register_22 (.D(Din), .en(demultiplexer_4_out5), .Q(register_22_q), .clk(clk));  // open: clr
  Register #(.width(32)) register_23 (.D(Din), .en(demultiplexer_5_out5), .Q(register_23_q), .clk(clk));  // open: clr
  Register #(.width(32)) register_24 (.D(Din), .en(demultiplexer_2_out5), .Q(register_24_q), .clk(clk));  // open: clr
  Register #(.width(32)) register_25 (.D(Din), .en(demultiplexer_4_out6), .Q(register_25_q), .clk(clk));  // open: clr
  Register #(.width(32)) register_26 (.D(Din), .en(demultiplexer_5_out6), .Q(register_26_q), .clk(clk));  // open: clr
  Register #(.width(32)) register_27 (.D(Din), .en(demultiplexer_2_out6), .Q(register_27_q), .clk(clk));  // open: clr
  Register #(.width(32)) register_28 (.D(Din), .en(demultiplexer_3_out6), .Q(register_28_q), .clk(clk));  // open: clr
  Register #(.width(32)) register_29 (.D(Din), .en(demultiplexer_3_out7), .Q(register_29_q), .clk(clk));  // open: clr
  Register #(.width(32)) register_30 (.D(Din), .en(demultiplexer_4_out7), .Q(register_30_q), .clk(clk));  // open: clr
  Register #(.width(32)) register_31 (.D(Din), .en(demultiplexer_5_out7), .Q(ra), .clk(clk));  // open: clr
  Register #(.width(32)) register_32 (.D(Din), .en(demultiplexer_2_out7), .Q(register_32_q), .clk(clk));  // open: clr
  Multiplexer #(.select(5), .width(32)) multiplexer_1 (
    .in0(register_3_q), .in1(register_5_q), .in2(v0), .in3(register_13_q), .in4(register_17_q),
    .in5(register_24_q), .in6(register_27_q), .in7(register_32_q), .in8(register_4_q), .in9(register_6_q),
    .in10(register_12_q), .in11(register_14_q), .in12(register_18_q), .in13(register_21_q),
    .in14(register_28_q), .in15(register_29_q), .in16(s0), .in17(s1), .in18(s2), .in19(register_15_q),
    .in20(register_19_q), .in21(register_22_q), .in22(register_25_q), .in23(register_30_q),
    .in24(register_2_q), .in25(register_8_q), .in26(register_10_q), .in27(register_16_q),
    .in28(register_20_q), .in29(register_23_q), .in30(register_26_q), .in31(ra), .out(R1), .sel(R1A));
  Multiplexer #(.select(5), .width(32)) multiplexer_2 (
    .in0(register_3_q), .in1(register_5_q), .in2(v0), .in3(register_13_q), .in4(register_17_q),
    .in5(register_24_q), .in6(register_27_q), .in7(register_32_q), .in8(register_4_q), .in9(register_6_q),
    .in10(register_12_q), .in11(register_14_q), .in12(register_18_q), .in13(register_21_q),
    .in14(register_28_q), .in15(register_29_q), .in16(s0), .in17(s1), .in18(s2), .in19(register_15_q),
    .in20(register_19_q), .in21(register_22_q), .in22(register_25_q), .in23(register_30_q),
    .in24(register_2_q), .in25(register_8_q), .in26(register_10_q), .in27(register_16_q),
    .in28(register_20_q), .in29(register_23_q), .in30(register_26_q), .in31(ra), .out(R2), .sel(R2A));

  // Other names for the same wires on the sheet: reg1[31:0] = R1; reg1A[4:0] = R1A; reg2[31:0] = R2; reg2A[4:0] = R2A;
  //   write_data[31:0] = Din; write_reg[4:0] = RW

  // Notes on the sheet:
  //   Input
  //   $0
  //   Output
  //   $Zero
  //   $1
  //   $at
  //   $2
  //   $v0
  //   $3
  //   $v1
  //   $4
  //   $a0
  //   $5
  //   $a1
  //   $6
  //   $a2
  //   $a3
  //   $7
endmodule
